# Fritzing sketch Rotating_Table (saved by Fritzing 0.9.5d)
breadboards: 1

parts:
  S1 = Pushbutton [package="[THT]"]
  S2 = Pushbutton [package="[THT]"]
  S3 = Pushbutton [package="[THT]"]
  LED1 = LED - 5mm [color="Red (633nm)" package="5 mm [THT]"]
  LED2 = LED - 5mm [color="Green (555nm)" package="5 mm [THT]"]
  Part1 = Arduino Nano (Rev3.0)
  R2 = Resistor [tolerance=±5% resistance=100 package=THT]
  R1 = Resistor [tolerance=±5% resistance=100 package=THT]
  R3 = Resistor [tolerance=±5% resistance=100 package=THT]
  X1 = X113647 Stepper Driver Board [package=board]
  MOTOR1 = 28BYJ-48 Stepper Motor
  LED3 = LED - 5mm [color="Infrared (940nm)" package="5 mm [THT]"]
  R4 = Trimmer Potentiometer [maximum_resistance=10kΩ package=THT]
  LCD1 = LCD screen
  Power_plug1 = Power plug

nets (from the breadboard view):
  N1: S1.Pin_1, S1.Pin_2, Part1.D10
  N2: S1.Pin_3, S1.Pin_4
  N3: S2.Pin_1, S2.Pin_2, Part1.D12/MISO
  GND: S2.Pin_3, S2.Pin_4, S3.Pin_3, S3.Pin_4, LED1.cathode, LED2.cathode, Part1.GND, X1.GND, LED3.cathode, R4.leg2, LCD1.VSS, LCD1.R/W, LCD1.LED-, Power_plug1.GND
  N4: S3.Pin_1, S3.Pin_2, Part1.D11/MOSI
  N5: LED1.anode, R1.Pin_0
  N6: LED2.anode, R2.Pin_0
  N7: Part1.D2, X1.IN1
  N8: Part1.D3, X1.IN2
  N9: Part1.D4, X1.IN3
  N10: Part1.D5, X1.IN4
  N11: Part1.D7, R2.Pin_1
  N12: Part1.D8, R1.Pin_1
  N13: Part1.D9, R3.Pin_1
  5V: Part1.5V, X1.+V, R4.leg1, LCD1.VDD, LCD1.LED+, Power_plug1.VCC
  N14: Part1.A5, LCD1.DB7
  N15: Part1.A4, LCD1.DB6
  N16: Part1.A3, LCD1.DB5
  N17: Part1.A2, LCD1.DB4
  N18: Part1.A1, LCD1.E
  N19: Part1.A0, LCD1.RS
  N20: R3.Pin_0, LED3.anode
  N21: X1.BLUE, MOTOR1.BLUE
  N22: X1.PINK, MOTOR1.PINK
  N23: X1.YELLOW, MOTOR1.YELLOW
  N24: X1.ORANGE, MOTOR1.ORANGE
  N25: X1.RED, MOTOR1.RED
  N26: R4.wiper, LCD1.V0

custom parts:
  X113647 Stepper Driver Board: A common stepper motor driver board based on ULN2003APG darlington array
  28BYJ-48 Stepper Motor: 28BYJ-48 gear-reduction stepper motor (small)

// code stored in the sketch: 3Dscan.ino
#include <LiquidCrystal.h>
#include <multiCameraIrControl.h>
#include <AccelStepper.h>

#define HALFSTEP   8 // Halfstep (4096 Steps per output shaft revolution)
#define motorPin1  2 // To ULN2003 driver Pin 1
#define motorPin2  3 // To ULN2003 driver Pin 2
#define motorPin3  4 // To ULN2003 driver Pin 3
#define motorPin4  5 // To ULN2003 driver Pin 4
#define lgr 7     // Led Green 
#define lro 8     // Led Red
#define B_up 10   // Button up 
#define B_down 11 // Button Down
#define B_ent 12  // Enter Button

int steps = 16; // Set to 16 by default Value
int pos = 0;    // Position of the Stepper
int zyk = 0;    // Cycle is running when 1
int E_val= 0;   // Entered Value of Steps (8,16,32 or 64)
int step_nr = 0; // The number of the actual processing Step

Nikon D5000(9); // 940nm IR-LED (PWM pin)
LiquidCrystal lcd(14, 15, 16, 17, 18, 19);
AccelStepper stepper(HALFSTEP, motorPin1, motorPin3, motorPin2, motorPin4);

void setup() 
{   
    pinMode(B_up, INPUT_PULLUP);
    pinMode(B_down, INPUT_PULLUP);
    pinMode(B_ent, INPUT_PULLUP);
    pinMode(lgr, OUTPUT);
    pinMode(lro, OUTPUT);
    stepper.setMaxSpeed(1200.0);    //Stepper Maxspeed
    stepper.setAcceleration(200.0); //Stepper Acceleration
    stepper.setSpeed(800);          // Stepper Speed
    lcd.begin(16, 2);               // LCD 16 Columns 2 Rows
    lcd.setCursor(4,0);
    lcd.print ("3D Scan");
    lcd.setCursor(4,1);
    lcd.print("By Bob M.");
    delay(3000);
    lcd.clear();
    lcd.print ("Number of Steps:");
    lcd.noCursor();
}

void loop() 
{ 
  if (digitalRead(B_ent) == 0) // Starting the cycle
  {
      zyk = 1 ;
  }
  
  if(digitalRead(B_up) == LOW && steps < 64 && zyk == 0) // Changing the value of the steps to make (Max. set to 64 but you can change the value)
    {
      steps = steps * 2; 
        
  while (digitalRead(B_up) == LOW); 
    }
    
  if(digitalRead(B_down) == LOW && steps > 16 && zyk == 0) // Changing the value of the steps to make (Min. set to 8 but you can change the value)
    {  
      steps = steps / 2;
      
    while (digitalRead(B_down) == LOW);
    }
    
  if (zyk == 1)                                      // LCD Progress of the steps
  {
    lcd.setCursor(5,1);
    lcd.print(step_nr);
    lcd.print("/"); 
    lcd.print(steps);
  }
    else                                            // LCD choice of how many Steps
    {
     lcd.setCursor(7,1);
     lcd.print(steps);
    }
  if (stepper.currentPosition() < 4095 && zyk == 1)
  {
    stepper.runToNewPosition(pos);                
    delay(1000);
    D5000.shutterNow();                             //Signal to IR-LED to take a picture
    delay(3000);
    E_val = (4096 / steps);                         // Calculation to know how many steps the stepper has to make
    pos = pos + E_val;                              // Calculation to know the new position for the next step
    step_nr = step_nr +1;                           // How many steps were made
   
  }
  if (stepper.currentPosition() >= 4096)            // Resetting the parameters for a new cycle
  {
    zyk = 0;
    pos = 0;
    stepper.setCurrentPosition(0);
    step_nr = 0;
    lcd.clear();
    lcd.setCursor(6,0);
    lcd.print("DONE");
    delay(2000);
    lcd.clear();
    lcd.home();
    lcd.print ("Number of Steps:");
  }
  if (zyk == 0)                                     //Ready LED
  {
    digitalWrite(lgr, HIGH);
    digitalWrite(lro, LOW);
    step_nr == 0;
  }
  if (zyk == 1)                     //In Progress LED
  {
    digitalWrite(lro, HIGH);
    digitalWrite(lgr, LOW);
  }
  
      
}
